// Logisim project SPM.circ as structural Verilog: 1 circuit, main circuit main
module main (
  input  y__serial_in,
  input  reset,
  input  x0,
  input  x1,
  input  x2,
  input  x3,
  input  x4,
  input  x5,
  input  x6,
  input  x7,
  output serial_output
);

  wire adder_1_out, adder_2_out, adder_3_out, adder_4_out, adder_5_out, adder_6_out, adder_7_out, and_1_out,
       and_2_out, and_3_out, and_4_out, and_5_out, and_6_out, and_7_out, clock_1_out, d_ff_2_q, d_ff_3_q,
       d_ff_4_q, d_ff_5_q, d_ff_6_q, d_ff_7_q, undriven;

  and and_1 (and_1_out, x0, y__serial_in);
  and and_2 (and_2_out, x1, y__serial_in);
  and and_3 (and_3_out, x2, y__serial_in);
  and and_4 (and_4_out, x3, y__serial_in);
  and and_5 (and_5_out, x4, y__serial_in);
  and and_6 (and_6_out, x5, x5, y__serial_in);
  and and_7 (and_7_out, x6, y__serial_in);
  // AND_Gate and_8 has open pins: in1=x7, in2=y__serial_in, out=open
  Adder #(.width(1)) adder_1 (.a(d_ff_2_q), .b(and_1_out), .out(adder_1_out));  // open: cin, cout
  Adder #(.width(1)) adder_2 (.a(and_2_out), .b(d_ff_3_q), .out(adder_2_out));  // open: cin, cout
  Adder #(.width(1)) adder_3 (.a(and_3_out), .b(d_ff_4_q), .out(adder_3_out));  // open: cin, cout
  Adder #(.width(1)) adder_4 (.a(and_4_out), .b(d_ff_5_q), .out(adder_4_out));  // open: cin, cout
  Adder #(.width(1)) adder_5 (.a(and_5_out), .b(d_ff_6_q), .out(adder_5_out));  // open: cin, cout
  Adder #(.width(1)) adder_6 (.a(and_6_out), .b(d_ff_7_q), .out(adder_6_out));  // open: cin, cout
  Adder #(.width(1)) adder_7 (.a(and_7_out), .b(undriven), .out(adder_7_out));  // open: cin, cout
  Clock clock_1 (.out(clock_1_out));
  D_Flip_Flop #(.trigger("high")) d_ff_1 (
    .clk(clock_1_out), .D(adder_1_out), .Q(serial_output), .reset(reset));  // open: Qn, preset, en
  D_Flip_Flop #(.trigger("high")) d_ff_2 (
    .clk(clock_1_out), .D(adder_2_out), .Q(d_ff_2_q), .reset(reset));  // open: Qn, preset, en
  D_Flip_Flop #(.trigger("high")) d_ff_3 (
    .clk(clock_1_out), .D(adder_3_out), .Q(d_ff_3_q), .reset(reset));  // open: Qn, preset, en
  D_Flip_Flop #(.trigger("high")) d_ff_4 (
    .clk(clock_1_out), .D(adder_4_out), .Q(d_ff_4_q), .reset(reset));  // open: Qn, preset, en
  D_Flip_Flop #(.trigger("high")) d_ff_5 (
    .clk(clock_1_out), .D(adder_5_out), .Q(d_ff_5_q), .reset(reset));  // open: Qn, preset, en
  D_Flip_Flop #(.trigger("high")) d_ff_6 (
    .clk(clock_1_out), .D(adder_6_out), .Q(d_ff_6_q), .reset(reset));  // open: Qn, preset, en
  D_Flip_Flop #(.trigger("high")) d_ff_7 (
    .clk(clock_1_out), .D(adder_7_out), .Q(d_ff_7_q), .reset(reset));  // open: Qn, preset, en
  _7_Segment_Display u_7_segment_display_1 ();  // open: g, f, a, b, e, d, c, dp

  // Notes on the sheet:
  //   from TCMP
endmodule
